# Fritzing sketch scchéma prototype (saved by Fritzing 0.9.3b)
breadboards: 1

parts:
  Composant1 = Arduino Uno (Rev3)
  R1 = Resistor [tolerance=±5% resistance=10k package=THT]
  R2 = Resistor [tolerance=±5% resistance=1M package=THT]
  R3 = Resistor [tolerance=±5% resistance=3.3k package=THT]
  L1 = Inductor [package="400 mil [THT]"]
  C1 = Ceramic Capacitor [capacitance=0.1nF package="100 mil [THT, multilayer]"]
  C2 = Ceramic Capacitor [capacitance=10nF package="100 mil [THT, multilayer]"]
  D1 = Rectifier Diode [part_number=1N4001 package="300 mil [THT]"]
  R4 = Resistor [tolerance=±5% resistance=220 package=THT]
  R5 = Resistor [tolerance=±5% resistance=220 package=THT]
  R6 = Resistor [tolerance=±5% resistance=220 package=THT]
  LED2 = LED - 5mm [color="Blue (525nm)" package="5 mm [THT]"]
  LED1 = LED - 5mm [color="Green (555nm)" package="5 mm [THT]"]
  LED3 = LED - 5mm [color="Red (633nm)" package="5 mm [THT]"]
  U1 = TOUCH [package=touch1]  # not connected

nets:
  N1: Composant1.A0, R2.Pin_0, C1.0, D1.cathode
  N2: Composant1.D9_PWM, R1.Pin_1
  N3: Composant1.D2, R5.Pin_1
  N4: Composant1.D3_PWM, R4.Pin_1
  N5: Composant1.D4, R6.Pin_1
  N6: Composant1.GND, R2.Pin_1, R3.Pin_1, C1.1, LED2.cathode, LED1.cathode, LED3.cathode
  N7: R1.Pin_0, R3.Pin_0, L1.pin_0
  N8: L1.pin_1, C2.1
  N9: C2.0, D1.anode
  N10: R4.Pin_0, LED1.anode
  N11: R5.Pin_0, LED2.anode
  N12: R6.Pin_0, LED3.anode

notes:
  patate
